# Fritzing sketch OrigamiBot (saved by Fritzing 0.9.3b)
breadboards: 2

parts:
  Q1 = NPN-Transistor [part_number=BC547 package="TO92 [THT]"]
  R2 = Photocell (LDR) [package=THT]
  R3 = Rotary Potentiometer (Large) [maximum_resistance=100kΩ package=THT]
  VCC1 = Battery block 9V
  S1 = Toggle Switch [package=THT]
  R4 = Resistor [tolerance=±5% resistance=10k package=THT]
  M1 = DC Motor
  LED1 = LED - 5mm [color="White (4500K)" package="5 mm [THT]"]
  LED2 = LED - 5mm [color="White (4500K)" package="5 mm [THT]"]
  R5 = Resistor [tolerance=±5% resistance=220 package=THT]

nets:
  N1: Q1.E, VCC1.-
  N2: Q1.B, R4.Pin_1
  N3: Q1.C, M1.pin_2
  N4: R2.pin_0, R3.wiper, R4.Pin_0
  N5: R2.pin_1, S1.L2, M1.pin_1
  N6: VCC1.+, S1.COM
  N7: LED1.cathode, LED2.cathode
  N8: LED1.anode, R5.Pin_0
