# Fritzing sketch Wakawaka (saved by Fritzing 0.9.3b)
breadboards: 1

parts:
  Part1 = Arduino Uno (Rev3) - ICSP
  J2 = Basic Servo
  HC-SR04_Sensor_1 = HC-SR04 Ultrasonic Distance Sensor
  J3 = Basic Servo

nets:
  N1: Part1.D9_PWM, J2.pulse
  N2: Part1.D10_PWM/SS, J3.pulse
  N3: Part1.D6_PWM, HC-SR04_Sensor_1.TRIG
  N4: Part1.D7, HC-SR04_Sensor_1.ECHO
  VCC: Part1.5V, J2.vcc, HC-SR04_Sensor_1.VCC
  GND: Part1.GND, J2.gnd, HC-SR04_Sensor_1.GND, J3.gnd
